# Fritzing sketch circuit_layout (saved by Fritzing 0.7.12b)
breadboards: 1

parts:
  R1 = Resistor [tolerance=±5% resistance=220 package=THT]
  3_PIN_FAN = male pin header, 3 pins [form="♂ (male)"]
  Pi1 = Adafruit Pi Cobbler
  Q1 = NPN-Transistor [part_number=BC635 package="TO92 [THT]"]

nets (from the pcb view):
  N1: R1.Pin_0, Pi1.#18
  N2: R1.Pin_1, Q1.B
  N3: 3_PIN_FAN.pin1, Pi1.#17
  N4: 3_PIN_FAN.pin2, Pi1.5V0
  N5: 3_PIN_FAN.pin3, Q1.E
  N6: Pi1.GND, Q1.C

notes:
  3 PIN 5V Fan

custom parts:
  Adafruit Pi Cobbler: Adafruit Pi Cobbler GPIO Breakout for Raspberry Pi
